// Logisim project _L0_CRC.circ as structural Verilog: 3 circuits, main circuit CRC
module CRC (
  input  [7:0] A,
  input  [3:0] B,
  output [10:0] out_3
);

  wire [2:0] mod_1_c;
  wire [3:0] func_1_d, func_2_d, func_3_d, func_4_d, func_5_d, func_6_d, func_7_d;
  wire [10:0] bit_extender_1_out, bit_extender_2_out, shifter_1_out;

  assign bit_extender_1_out = {{3{1'b0}}, A};  // Bit_Extender bit_extender_1
  // Probe on shifter_1_out
  Shifter #(.width(11)) shifter_1 (.in(bit_extender_1_out), .\dist (4'b0011), .out(shifter_1_out));
  FUNC func_1 (.A(func_2_d), .B(B), .C(shifter_1_out[5]), .D(func_1_d));
  FUNC func_2 (.A(shifter_1_out[10:7]), .B(B), .C(shifter_1_out[6]), .D(func_2_d));
  FUNC func_3 (.A(func_4_d), .B(B), .C(shifter_1_out[3]), .D(func_3_d));
  FUNC func_4 (.A(func_1_d), .B(B), .C(shifter_1_out[4]), .D(func_4_d));
  FUNC func_5 (.A(func_3_d), .B(B), .C(shifter_1_out[2]), .D(func_5_d));
  FUNC func_6 (.A(func_7_d), .B(B), .C(shifter_1_out[0]), .D(func_6_d));
  FUNC func_7 (.A(func_5_d), .B(B), .C(shifter_1_out[1]), .D(func_7_d));
  MOD mod_1 (.A(func_6_d), .B(B), .C(mod_1_c));  // open: D
  assign bit_extender_2_out = {{8{1'b0}}, mod_1_c};  // Bit_Extender bit_extender_2
  assign out_3 = shifter_1_out ^ bit_extender_2_out;  // XOR_Gate xor_1, 11 bits wide
endmodule

module MOD (
  input  [3:0] A,
  input  [3:0] B,
  output D,
  output [2:0] C
);

  wire [2:0] xor_1_out;

  assign xor_1_out = A[2:0] ^ B[2:0];  // XOR_Gate xor_1, 3 bits wide
  Multiplexer #(.width(3), .enable("false")) multiplexer_1 (.in0(A[2:0]), .in1(xor_1_out), .out(C), .sel(A[3]));

  assign D = A[3];
endmodule

module FUNC (
  input  [3:0] A,
  input  [3:0] B,
  input  C,
  output [3:0] D
);

  wire [2:0] mod_1_c;
  wire [3:0] bit_extender_1_out, bit_extender_2_out, shifter_1_out;

  MOD mod_1 (.A(A), .B(B), .C(mod_1_c));  // open: D
  assign bit_extender_1_out = {{3{1'b0}}, C};  // Bit_Extender bit_extender_1
  assign bit_extender_2_out = {{1{1'b0}}, mod_1_c};  // Bit_Extender bit_extender_2
  Shifter #(.width(4)) shifter_1 (.in(bit_extender_2_out), .\dist (2'b01), .out(shifter_1_out));
  assign D = shifter_1_out ^ bit_extender_1_out;  // XOR_Gate xor_1, 4 bits wide
endmodule
