// Logisim project _L0_FSM.circ as structural Verilog: 2 circuits, main circuit fsm
module fsm (
  input  CLR,
  input  [1:0] In_1_0,
  output Z
);

  wire and_1_out, and_2_out, circ_1_t0, circ_1_t1, clock_1_out, s0_q, s1_q;

  circ circ_1 (.S1(s1_q), .S0(s0_q), .I1(In_1_0[1]), .I0(In_1_0[0]), .T1(circ_1_t1), .T0(circ_1_t0), .Y(Z));
  and and_1 (and_1_out, circ_1_t0, ~CLR);  // AND_Gate
  and and_2 (and_2_out, circ_1_t1, ~CLR);  // AND_Gate
  Register #(.width(1)) s0 (.D(and_1_out), .Q(s0_q), .clk(clock_1_out));  // open: en, clr
  Register #(.width(1)) s1 (.D(and_2_out), .Q(s1_q), .clk(clock_1_out));  // open: en, clr
  Clock clock_1 (.out(clock_1_out));
endmodule

module circ (
  input  S1,
  input  S0,
  input  I1,
  input  I0,
  output T1,
  output T0,
  output Y
);

  wire not_1_out, not_2_out, not_3_out, not_4_out;

  and and_1 (T1, S0, not_1_out);
  not not_1 (not_1_out, I0);
  not not_2 (not_2_out, S1);
  not not_3 (not_3_out, I1);
  and and_2 (T0, not_2_out, not_3_out, I0);
  and and_3 (Y, S1, not_4_out);
  not not_4 (not_4_out, I0);
endmodule
