// Logisim project _L0_GRF.circ as structural Verilog: 1 circuit, main circuit grf
module grf (
  input  reset,
  input  clk,
  input  WE,
  input  [31:0] WD,
  input  [4:0] A3,
  input  [4:0] A2,
  input  [4:0] A1,
  output [31:0] RD2,
  output [31:0] RD1
);

  wire I00, I01, I02, I03, I04, I05, I06, I07, I08, I09, I10, I11, I12, I13, I14, I15, I16, I17, I18, I19,
       I20, I21, I22, I23, I24, I25, I26, I27, I28, I29, I30, I31;
  wire [31:0] multiplexer_1_out, multiplexer_2_out, multiplexer_3_out, multiplexer_4_out, multiplexer_5_out,
       multiplexer_6_out, multiplexer_7_out, multiplexer_8_out, multiplexer_9_out, multiplexer_10_out,
       multiplexer_11_out, multiplexer_12_out, multiplexer_13_out, multiplexer_14_out, multiplexer_15_out,
       multiplexer_16_out, multiplexer_17_out, multiplexer_18_out, multiplexer_19_out, multiplexer_20_out,
       multiplexer_21_out, multiplexer_22_out, multiplexer_23_out, multiplexer_24_out, multiplexer_25_out,
       multiplexer_26_out, multiplexer_27_out, multiplexer_28_out, multiplexer_29_out, multiplexer_30_out,
       multiplexer_31_out, multiplexer_32_out, O00, O01, O02, O03, O04, O05, O06, O07, O08, O09, O10, O11,
       O12, O13, O14, O15, O16, O17, O18, O19, O20, O21, O22, O23, O24, O25, O26, O27, O28, O29, O30, O31;

  Multiplexer #(.width(32), .enable("false")) multiplexer_1 (.in0(O00), .in1(WD), .out(multiplexer_1_out), .sel(I00));
  Multiplexer #(.width(32), .enable("false")) multiplexer_2 (.in0(O04), .in1(WD), .out(multiplexer_2_out), .sel(I04));
  Multiplexer #(.width(32), .enable("false")) multiplexer_3 (.in0(O08), .in1(WD), .out(multiplexer_3_out), .sel(I08));
  Multiplexer #(.width(32), .enable("false")) multiplexer_4 (.in0(O12), .in1(WD), .out(multiplexer_4_out), .sel(I12));
  Multiplexer #(.width(32), .enable("false")) multiplexer_5 (.in0(O16), .in1(WD), .out(multiplexer_5_out), .sel(I16));
  Multiplexer #(.width(32), .enable("false")) multiplexer_6 (.in0(O20), .in1(WD), .out(multiplexer_6_out), .sel(I20));
  Multiplexer #(.width(32), .enable("false")) multiplexer_7 (.in0(O24), .in1(WD), .out(multiplexer_7_out), .sel(I24));
  Multiplexer #(.width(32), .enable("false")) multiplexer_8 (.in0(O28), .in1(WD), .out(multiplexer_8_out), .sel(I28));
  Register #(.width(32)) R00 (.D(multiplexer_1_out), .en(WE), .Q(O00), .clk(clk), .clr(1'b1));
  Register #(.width(32)) R04 (.D(multiplexer_2_out), .en(WE), .Q(O04), .clk(clk), .clr(reset));
  Register #(.width(32)) R08 (.D(multiplexer_3_out), .en(WE), .Q(O08), .clk(clk), .clr(reset));
  Register #(.width(32)) R12 (.D(multiplexer_4_out), .en(WE), .Q(O12), .clk(clk), .clr(reset));
  Register #(.width(32)) R16 (.D(multiplexer_5_out), .en(WE), .Q(O16), .clk(clk), .clr(reset));
  Register #(.width(32)) R20 (.D(multiplexer_6_out), .en(WE), .Q(O20), .clk(clk), .clr(reset));
  Register #(.width(32)) R24 (.D(multiplexer_7_out), .en(WE), .Q(O24), .clk(clk), .clr(reset));
  Register #(.width(32)) R28 (.D(multiplexer_8_out), .en(WE), .Q(O28), .clk(clk), .clr(reset));
  Multiplexer #(.width(32), .enable("false")) multiplexer_9 (.in0(O01), .in1(WD), .out(multiplexer_9_out), .sel(I01));
  Multiplexer #(.width(32), .enable("false")) multiplexer_10 (.in0(O05), .in1(WD), .out(multiplexer_10_out), .sel(I05));
  Multiplexer #(.width(32), .enable("false")) multiplexer_11 (.in0(O09), .in1(WD), .out(multiplexer_11_out), .sel(I09));
  Multiplexer #(.width(32), .enable("false")) multiplexer_12 (.in0(O13), .in1(WD), .out(multiplexer_12_out), .sel(I13));
  Multiplexer #(.width(32), .enable("false")) multiplexer_13 (.in0(O17), .in1(WD), .out(multiplexer_13_out), .sel(I17));
  Multiplexer #(.width(32), .enable("false")) multiplexer_14 (.in0(O21), .in1(WD), .out(multiplexer_14_out), .sel(I21));
  Multiplexer #(.width(32), .enable("false")) multiplexer_15 (.in0(O25), .in1(WD), .out(multiplexer_15_out), .sel(I25));
  Multiplexer #(.width(32), .enable("false")) multiplexer_16 (.in0(O29), .in1(WD), .out(multiplexer_16_out), .sel(I29));
  Register #(.width(32)) R01 (.D(multiplexer_9_out), .en(WE), .Q(O01), .clk(clk), .clr(reset));
  Register #(.width(32)) R05 (.D(multiplexer_10_out), .en(WE), .Q(O05), .clk(clk), .clr(reset));
  Register #(.width(32)) R09 (.D(multiplexer_11_out), .en(WE), .Q(O09), .clk(clk), .clr(reset));
  Register #(.width(32)) R13 (.D(multiplexer_12_out), .en(WE), .Q(O13), .clk(clk), .clr(reset));
  Register #(.width(32)) R17 (.D(multiplexer_13_out), .en(WE), .Q(O17), .clk(clk), .clr(reset));
  Register #(.width(32)) R21 (.D(multiplexer_14_out), .en(WE), .Q(O21), .clk(clk), .clr(reset));
  Register #(.width(32)) R25 (.D(multiplexer_15_out), .en(WE), .Q(O25), .clk(clk), .clr(reset));
  Register #(.width(32)) R29 (.D(multiplexer_16_out), .en(WE), .Q(O29), .clk(clk), .clr(reset));
  Register #(.width(32)) R02 (.D(multiplexer_17_out), .en(WE), .Q(O02), .clk(clk), .clr(reset));
  Multiplexer #(.width(32), .enable("false")) multiplexer_17 (.in0(O02), .in1(WD), .out(multiplexer_17_out), .sel(I02));
  Multiplexer #(.width(32), .enable("false")) multiplexer_18 (.in0(O06), .in1(WD), .out(multiplexer_18_out), .sel(I06));
  Register #(.width(32)) R06 (.D(multiplexer_18_out), .en(WE), .Q(O06), .clk(clk), .clr(reset));
  Multiplexer #(.width(32), .enable("false")) multiplexer_19 (.in0(O10), .in1(WD), .out(multiplexer_19_out), .sel(I10));
  Register #(.width(32)) R10 (.D(multiplexer_19_out), .en(WE), .Q(O10), .clk(clk), .clr(reset));
  Register #(.width(32)) R14 (.D(multiplexer_20_out), .en(WE), .Q(O14), .clk(clk), .clr(reset));
  Multiplexer #(.width(32), .enable("false")) multiplexer_20 (.in0(O14), .in1(WD), .out(multiplexer_20_out), .sel(I14));
  Register #(.width(32)) R18 (.D(multiplexer_21_out), .en(WE), .Q(O18), .clk(clk), .clr(reset));
  Multiplexer #(.width(32), .enable("false")) multiplexer_21 (.in0(O18), .in1(WD), .out(multiplexer_21_out), .sel(I18));
  Multiplexer #(.width(32), .enable("false")) multiplexer_22 (.in0(O22), .in1(WD), .out(multiplexer_22_out), .sel(I22));
  Register #(.width(32)) R22 (.D(multiplexer_22_out), .en(WE), .Q(O22), .clk(clk), .clr(reset));
  Register #(.width(32)) R26 (.D(multiplexer_23_out), .en(WE), .Q(O26), .clk(clk), .clr(reset));
  Multiplexer #(.width(32), .enable("false")) multiplexer_23 (.in0(O26), .in1(WD), .out(multiplexer_23_out), .sel(I26));
  Multiplexer #(.width(32), .enable("false")) multiplexer_24 (.in0(O30), .in1(WD), .out(multiplexer_24_out), .sel(I30));
  Register #(.width(32)) R30 (.D(multiplexer_24_out), .en(WE), .Q(O30), .clk(clk), .clr(reset));
  Multiplexer #(.width(32), .enable("false")) multiplexer_25 (.in0(O03), .in1(WD), .out(multiplexer_25_out), .sel(I03));
  Multiplexer #(.width(32), .enable("false")) multiplexer_26 (.in0(O07), .in1(WD), .out(multiplexer_26_out), .sel(I07));
  Multiplexer #(.width(32), .enable("false")) multiplexer_27 (.in0(O11), .in1(WD), .out(multiplexer_27_out), .sel(I11));
  Multiplexer #(.width(32), .enable("false")) multiplexer_28 (.in0(O15), .in1(WD), .out(multiplexer_28_out), .sel(I15));
  Multiplexer #(.width(32), .enable("false")) multiplexer_29 (.in0(O19), .in1(WD), .out(multiplexer_29_out), .sel(I19));
  Multiplexer #(.width(32), .enable("false")) multiplexer_30 (.in0(O23), .in1(WD), .out(multiplexer_30_out), .sel(I23));
  Multiplexer #(.width(32), .enable("false")) multiplexer_31 (.in0(O27), .in1(WD), .out(multiplexer_31_out), .sel(I27));
  Multiplexer #(.width(32), .enable("false")) multiplexer_32 (.in0(O31), .in1(WD), .out(multiplexer_32_out), .sel(I31));
  Register #(.width(32)) R03 (.D(multiplexer_25_out), .en(WE), .Q(O03), .clk(clk), .clr(reset));
  Register #(.width(32)) R07 (.D(multiplexer_26_out), .en(WE), .Q(O07), .clk(clk), .clr(reset));
  Register #(.width(32)) R11 (.D(multiplexer_27_out), .en(WE), .Q(O11), .clk(clk), .clr(reset));
  Register #(.width(32)) R15 (.D(multiplexer_28_out), .en(WE), .Q(O15), .clk(clk), .clr(reset));
  Register #(.width(32)) R19 (.D(multiplexer_29_out), .en(WE), .Q(O19), .clk(clk), .clr(reset));
  Register #(.width(32)) R23 (.D(multiplexer_30_out), .en(WE), .Q(O23), .clk(clk), .clr(reset));
  Register #(.width(32)) R27 (.D(multiplexer_31_out), .en(WE), .Q(O27), .clk(clk), .clr(reset));
  Register #(.width(32)) R31 (.D(multiplexer_32_out), .en(WE), .Q(O31), .clk(clk), .clr(reset));
  Decoder #(.select(5), .enable("false")) decoder_1 (
    .out0(I00), .out1(I01), .out2(I02), .out3(I03), .out4(I04), .out5(I05), .out6(I06), .out7(I07),
    .out8(I08), .out9(I09), .out10(I10), .out11(I11), .out12(I12), .out13(I13), .out14(I14), .out15(I15),
    .out16(I16), .out17(I17), .out18(I18), .out19(I19), .out20(I20), .out21(I21), .out22(I22), .out23(I23),
    .out24(I24), .out25(I25), .out26(I26), .out27(I27), .out28(I28), .out29(I29), .out30(I30), .out31(I31),
    .sel(A3));
  Multiplexer #(.select(5), .width(32), .enable("false")) multiplexer_33 (
    .in0(O00), .in1(O01), .in2(O02), .in3(O03), .in4(O04), .in5(O05), .in6(O06), .in7(O07), .in8(O08),
    .in9(O09), .in10(O10), .in11(O11), .in12(O12), .in13(O13), .in14(O14), .in15(O15), .in16(O16),
    .in17(O17), .in18(O18), .in19(O19), .in20(O20), .in21(O21), .in22(O22), .in23(O23), .in24(O24),
    .in25(O25), .in26(O26), .in27(O27), .in28(O28), .in29(O29), .in30(O30), .in31(O31), .out(RD2), .sel(A2));
  Multiplexer #(.select(5), .width(32), .enable("false")) multiplexer_34 (
    .in0(O00), .in1(O01), .in2(O02), .in3(O03), .in4(O04), .in5(O05), .in6(O06), .in7(O07), .in8(O08),
    .in9(O09), .in10(O10), .in11(O11), .in12(O12), .in13(O13), .in14(O14), .in15(O15), .in16(O16),
    .in17(O17), .in18(O18), .in19(O19), .in20(O20), .in21(O21), .in22(O22), .in23(O23), .in24(O24),
    .in25(O25), .in26(O26), .in27(O27), .in28(O28), .in29(O29), .in30(O30), .in31(O31), .out(RD1), .sel(A1));
endmodule
