// Logisim project _L1_ftoi.circ as structural Verilog: 1 circuit, main circuit ftoi
module ftoi (
  input  [15:0] float,
  output [31:0] \int 
);

  wire comparator_1_eq, comparator_2_eq, or_1_out, subtractor_1_bout;
  wire [4:0] multiplexer_1_out, negator_1_out, subtractor_1_out;
  wire [10:0] bit_extender_1_out;
  wire [31:0] bit_extender_2_out, multiplexer_2_out, multiplexer_3_out, negator_2_out, shifter_1_out,
       shifter_2_out, shifter_3_out;

  Comparator #(.width(5)) comparator_1 (.a({5{1'b1}}), .b(float[14:10]), .eq(comparator_1_eq));  // open: gt, lt
  Comparator #(.width(5)) comparator_2 (.a(float[14:10]), .b({5{1'b0}}), .eq(comparator_2_eq));  // open: gt, lt
  assign bit_extender_1_out = {{1{1'b1}}, float[9:0]};  // Bit_Extender bit_extender_1
  assign bit_extender_2_out = {{21{1'b0}}, bit_extender_1_out};  // Bit_Extender bit_extender_2
  Subtractor #(.width(5)) subtractor_1 (
    .a(float[14:10]), .b(5'b01111), .out(subtractor_1_out), .bout(subtractor_1_bout));  // open: bin
  Negator #(.width(5)) negator_1 (.in(subtractor_1_out), .out(negator_1_out));
  Multiplexer #(.width(5), .enable("false")) multiplexer_1 (
    .in0(subtractor_1_out), .in1(negator_1_out), .out(multiplexer_1_out), .sel(subtractor_1_bout));
  Shifter #(.width(32)) shifter_1 (.in(bit_extender_2_out), .\dist (multiplexer_1_out), .out(shifter_1_out));
  Shifter #(.width(32), .shift("lr")) shifter_2 (
    .in(bit_extender_2_out), .\dist (multiplexer_1_out), .out(shifter_2_out));
  Multiplexer #(.width(32), .enable("false")) multiplexer_2 (
    .in0(shifter_1_out), .in1(shifter_2_out), .out(multiplexer_2_out), .sel(subtractor_1_bout));
  Shifter #(.width(32), .shift("lr")) shifter_3 (.in(multiplexer_2_out), .\dist (5'b01010), .out(shifter_3_out));
  Negator #(.width(32)) negator_2 (.in(shifter_3_out), .out(negator_2_out));
  Multiplexer #(.width(32), .enable("false")) multiplexer_3 (
    .in0(shifter_3_out), .in1(negator_2_out), .out(multiplexer_3_out), .sel(float[15]));
  or or_1 (or_1_out, comparator_1_eq, comparator_2_eq);
  Multiplexer #(.width(32), .enable("false")) multiplexer_4 (
    .in0(multiplexer_3_out), .in1({32{1'b0}}), .out(\int ), .sel(or_1_out));
endmodule
