// Logisim project _L1_navigation_2020.circ as structural Verilog: 2 circuits, main circuit navigation
module navigation (
  input  [1:0] dir,
  input  clk,
  input  reset,
  output arrive,
  output hit
);

  wire [3:0] circ_1_t0;
  wire [3:1] register_1_q;

  CIRC circ_1 (
    .s3(register_1_q[3]), .s2(register_1_q[2]), .s1(register_1_q[1]), .s0(hit), .i1(dir[1]), .i0(dir[0]),
    .t3(circ_1_t0[3]), .t2(circ_1_t0[2]), .t1(circ_1_t0[1]), .t0(circ_1_t0[0]));
  // Probe on {register_1_q, hit}
  // Probe on circ_1_t0
  Register #(.width(4)) register_1 (.D(circ_1_t0), .Q({register_1_q, hit}), .clk(clk), .clr(reset));  // open: en
  Comparator #(.width(3)) comparator_1 (.a(3'b100), .b(register_1_q), .eq(arrive));  // open: gt, lt
endmodule

module CIRC (
  input  s3,
  input  s2,
  input  s1,
  input  s0,
  input  i1,
  input  i0,
  output t3,
  output t2,
  output t1,
  output t0
);

  wire and_1_out, and_2_out, and_3_out, and_4_out, and_5_out, and_6_out, and_7_out, and_8_out, and_9_out,
       and_10_out, and_11_out, and_12_out, and_13_out, and_14_out, and_15_out, and_16_out, not_1_out,
       not_2_out, not_3_out, not_4_out, not_5_out, not_6_out, not_7_out, not_8_out, not_9_out, not_10_out,
       not_11_out, not_12_out, not_13_out, not_14_out, not_15_out, not_16_out, not_17_out, not_18_out,
       not_19_out, not_20_out, not_21_out, not_22_out, not_23_out, not_24_out, not_25_out, not_26_out,
       not_27_out, not_28_out;

  not not_1 (not_1_out, s1);
  not not_2 (not_2_out, i1);
  not not_3 (not_3_out, i0);
  not not_4 (not_4_out, i1);
  not not_5 (not_5_out, s2);
  not not_6 (not_6_out, i1);
  not not_7 (not_7_out, i1);
  not not_8 (not_8_out, i0);
  not not_9 (not_9_out, s1);
  not not_10 (not_10_out, i1);
  not not_11 (not_11_out, s1);
  not not_12 (not_12_out, i0);
  not not_13 (not_13_out, s3);
  not not_14 (not_14_out, s2);
  not not_15 (not_15_out, i1);
  not not_16 (not_16_out, i0);
  not not_17 (not_17_out, i0);
  not not_18 (not_18_out, s3);
  not not_19 (not_19_out, s1);
  not not_20 (not_20_out, i1);
  not not_21 (not_21_out, s3);
  not not_22 (not_22_out, s2);
  not not_23 (not_23_out, s1);
  not not_24 (not_24_out, s3);
  not not_25 (not_25_out, s1);
  not not_26 (not_26_out, i0);
  not not_27 (not_27_out, i1);
  not not_28 (not_28_out, i0);
  and and_1 (and_1_out, s2, not_1_out, not_2_out, not_3_out);
  and and_2 (and_2_out, s2, s1, not_4_out, i0);
  and and_3 (and_3_out, not_5_out, s1, not_6_out);
  and and_4 (and_4_out, s1, not_7_out, not_8_out);
  and and_5 (and_5_out, s2, not_9_out, not_10_out, i0);
  and and_6 (and_6_out, s2, not_11_out, i1, not_12_out);
  and and_7 (and_7_out, s2, s1, i1, i0);
  and and_8 (and_8_out, not_13_out, not_14_out, not_15_out, not_16_out);
  and and_9 (and_9_out, s1, i1, i0);
  and and_10 (and_10_out, s2, i1, i0);
  and and_11 (and_11_out, s2, s1, not_17_out);
  and and_12 (and_12_out, not_18_out, not_19_out, not_20_out, i0);
  and and_13 (and_13_out, not_21_out, not_22_out, not_23_out, i1);
  and and_14 (and_14_out, not_24_out, not_25_out, i1, not_26_out);
  and and_15 (and_15_out, s1, i1, i0);
  and and_16 (and_16_out, s2, s1, not_27_out, not_28_out);
  or or_1 (t3, and_1_out, and_2_out);
  or or_2 (t2, and_3_out, and_4_out, and_5_out, and_6_out, and_7_out);
  or or_3 (t1, and_8_out, and_9_out, and_10_out, and_11_out);
  or or_4 (t0, and_12_out, and_13_out, and_14_out, and_15_out, and_16_out);
endmodule
