// Logisim project cpu+j+xor.circ as structural Verilog: 13 circuits, main circuit main
module main (
  input  Rst,
  output [31:0] Instr,
  output [31:0] pc,
  output RegWrite,
  output [4:0] RegAddr,
  output [31:0] RegData,
  output MemWrite,
  output [31:0] MemAddr,
  output [31:0] MemData
);

  wire aluc_1_zero, clock_1_out, cu_1_alusrc, cu_1_isbyte, cu_1_jal, cu_1_jump, cu_1_memtoreg, cu_1_pcsrc,
       cu_1_regdst;
  wire [1:0] cu_1_extop;
  wire [2:0] cu_1_aluctrl;
  wire [4:0] splitter_1_rd, splitter_1_rs, splitter_1_rt, splitter_1_shamt;
  wire [5:0] splitter_1_funct, splitter_1_opcode;
  wire [15:0] splitter_1_imm;
  wire [25:0] splitter_1_addr;
  wire [31:0] aluc_1_alures, ext_1_extimm, grf_1_rd1;

  Clock clock_1 (.out(clock_1_out));
  IFU ifu_1 (
    .Clk(clock_1_out), .PCSrc(cu_1_pcsrc), .Rst(Rst), .SignImm(ext_1_extimm), .Instr(Instr), .pc(pc),
    .Jump(cu_1_jump), .JumpAddr(splitter_1_addr));
  Splitter splitter_1 (
    .Instr(Instr), .imm(splitter_1_imm), .addr(splitter_1_addr), .funct(splitter_1_funct),
    .shamt(splitter_1_shamt), .rd(splitter_1_rd), .rt(splitter_1_rt), .rs(splitter_1_rs),
    .Opcode(splitter_1_opcode));
  GRF grf_1 (
    .Clk(clock_1_out), .Rst(Rst), .RegWrite(RegWrite), .RegDst(cu_1_regdst), .WD(RegData), .RD1(grf_1_rd1),
    .RD2(MemData), .RA(RegAddr), .rs(splitter_1_rs), .rt(splitter_1_rt), .rd(splitter_1_rd), .jal(cu_1_jal));
  EXT ext_1 (.Imm(splitter_1_imm), .ExtOp(cu_1_extop), .ExtImm(ext_1_extimm));
  CU cu_1 (
    .ALUCtrl(cu_1_aluctrl), .PCSrc(cu_1_pcsrc), .EXTOp(cu_1_extop), .Opcode(splitter_1_opcode),
    .RegWrite(RegWrite), .RegDst(cu_1_regdst), .ALUSrc(cu_1_alusrc), .Zero(aluc_1_zero), .MemWrite(MemWrite),
    .MemtoReg(cu_1_memtoreg), .funct(splitter_1_funct), .Jump(cu_1_jump), .jal(cu_1_jal), .isByte(cu_1_isbyte));
  ALUC aluc_1 (
    .ALUCtrl(cu_1_aluctrl), .SrcA(grf_1_rd1), .Dat(MemData), .SignImm(ext_1_extimm), .ALUSrc(cu_1_alusrc),
    .Zero(aluc_1_zero), .ALURes(aluc_1_alures), .Shamt(splitter_1_shamt));
  DMC dmc_1 (
    .MemtoReg(cu_1_memtoreg), .Clk(clock_1_out), .MemWrite(MemWrite), .ALURes(aluc_1_alures),
    .WriteData(MemData), .Rst(Rst), .Result(RegData), .Addr(MemAddr), .jal(cu_1_jal), .PC(pc),
    .isByte(cu_1_isbyte));
endmodule

module GRF (
  input  jal,
  input  Clk,
  input  Rst,
  input  RegWrite,
  input  RegDst,
  input  [4:0] rs,
  input  [4:0] rt,
  input  [4:0] rd,
  input  [31:0] WD,
  output [31:0] RD1,
  output [31:0] RD2,
  output [4:0] RA
);

  wire [4:0] multiplexer_1_out;

  Multiplexer #(.width(5), .enable("false")) multiplexer_1 (.in0(rt), .in1(rd), .out(multiplexer_1_out), .sel(RegDst));
  Multiplexer #(.width(5), .enable("false")) multiplexer_2 (
    .in0(multiplexer_1_out), .in1({5{1'b1}}), .out(RA), .sel(jal));
  RF rf_1 (.RD2(RD2), .RD1(RD1), .WD(WD), .RegWrite(RegWrite), .Clk(Clk), .Rst(Rst), .A3(RA), .A2(rt), .A1(rs));
endmodule

module RF (
  input  Rst,
  input  Clk,
  input  RegWrite,
  input  [31:0] WD,
  input  [4:0] A3,
  input  [4:0] A2,
  input  [4:0] A1,
  output [31:0] RD2,
  output [31:0] RD1
);

  wire I00, I01, I02, I03, I04, I05, I06, I07, I08, I09, I10, I11, I12, I13, I14, I15, I16, I17, I18, I19,
       I20, I21, I22, I23, I24, I25, I26, I27, I28, I29, I30, I31;
  wire [31:0] multiplexer_1_out, multiplexer_2_out, multiplexer_3_out, multiplexer_4_out, multiplexer_5_out,
       multiplexer_6_out, multiplexer_7_out, multiplexer_8_out, multiplexer_9_out, multiplexer_10_out,
       multiplexer_11_out, multiplexer_12_out, multiplexer_13_out, multiplexer_14_out, multiplexer_15_out,
       multiplexer_16_out, multiplexer_17_out, multiplexer_18_out, multiplexer_19_out, multiplexer_20_out,
       multiplexer_21_out, multiplexer_22_out, multiplexer_23_out, multiplexer_24_out, multiplexer_25_out,
       multiplexer_26_out, multiplexer_27_out, multiplexer_28_out, multiplexer_29_out, multiplexer_30_out,
       multiplexer_31_out, multiplexer_32_out, O00, O01, O02, O03, O04, O05, O06, O07, O08, O09, O10, O11,
       O12, O13, O14, O15, O16, O17, O18, O19, O20, O21, O22, O23, O24, O25, O26, O27, O28, O29, O30, O31;

  Multiplexer #(.width(32), .enable("false")) multiplexer_1 (.in0(O00), .in1(WD), .out(multiplexer_1_out), .sel(I00));
  Multiplexer #(.width(32), .enable("false")) multiplexer_2 (.in0(O04), .in1(WD), .out(multiplexer_2_out), .sel(I04));
  Multiplexer #(.width(32), .enable("false")) multiplexer_3 (.in0(O08), .in1(WD), .out(multiplexer_3_out), .sel(I08));
  Multiplexer #(.width(32), .enable("false")) multiplexer_4 (.in0(O12), .in1(WD), .out(multiplexer_4_out), .sel(I12));
  Multiplexer #(.width(32), .enable("false")) multiplexer_5 (.in0(O16), .in1(WD), .out(multiplexer_5_out), .sel(I16));
  Multiplexer #(.width(32), .enable("false")) multiplexer_6 (.in0(O20), .in1(WD), .out(multiplexer_6_out), .sel(I20));
  Multiplexer #(.width(32), .enable("false")) multiplexer_7 (.in0(O24), .in1(WD), .out(multiplexer_7_out), .sel(I24));
  Multiplexer #(.width(32), .enable("false")) multiplexer_8 (.in0(O28), .in1(WD), .out(multiplexer_8_out), .sel(I28));
  Register #(.width(32)) R00 (.D(multiplexer_1_out), .en(RegWrite), .Q(O00), .clk(Clk), .clr(1'b1));
  Register #(.width(32)) R04 (.D(multiplexer_2_out), .en(RegWrite), .Q(O04), .clk(Clk), .clr(Rst));
  Register #(.width(32)) R08 (.D(multiplexer_3_out), .en(RegWrite), .Q(O08), .clk(Clk), .clr(Rst));
  Register #(.width(32)) R12 (.D(multiplexer_4_out), .en(RegWrite), .Q(O12), .clk(Clk), .clr(Rst));
  Register #(.width(32)) R16 (.D(multiplexer_5_out), .en(RegWrite), .Q(O16), .clk(Clk), .clr(Rst));
  Register #(.width(32)) R20 (.D(multiplexer_6_out), .en(RegWrite), .Q(O20), .clk(Clk), .clr(Rst));
  Register #(.width(32)) R24 (.D(multiplexer_7_out), .en(RegWrite), .Q(O24), .clk(Clk), .clr(Rst));
  Register #(.width(32)) R28 (.D(multiplexer_8_out), .en(RegWrite), .Q(O28), .clk(Clk), .clr(Rst));
  Multiplexer #(.width(32), .enable("false")) multiplexer_9 (.in0(O01), .in1(WD), .out(multiplexer_9_out), .sel(I01));
  Multiplexer #(.width(32), .enable("false")) multiplexer_10 (.in0(O05), .in1(WD), .out(multiplexer_10_out), .sel(I05));
  Multiplexer #(.width(32), .enable("false")) multiplexer_11 (.in0(O09), .in1(WD), .out(multiplexer_11_out), .sel(I09));
  Multiplexer #(.width(32), .enable("false")) multiplexer_12 (.in0(O13), .in1(WD), .out(multiplexer_12_out), .sel(I13));
  Multiplexer #(.width(32), .enable("false")) multiplexer_13 (.in0(O17), .in1(WD), .out(multiplexer_13_out), .sel(I17));
  Multiplexer #(.width(32), .enable("false")) multiplexer_14 (.in0(O21), .in1(WD), .out(multiplexer_14_out), .sel(I21));
  Multiplexer #(.width(32), .enable("false")) multiplexer_15 (.in0(O25), .in1(WD), .out(multiplexer_15_out), .sel(I25));
  Multiplexer #(.width(32), .enable("false")) multiplexer_16 (.in0(O29), .in1(WD), .out(multiplexer_16_out), .sel(I29));
  Register #(.width(32)) R01 (.D(multiplexer_9_out), .en(RegWrite), .Q(O01), .clk(Clk), .clr(Rst));
  Register #(.width(32)) R05 (.D(multiplexer_10_out), .en(RegWrite), .Q(O05), .clk(Clk), .clr(Rst));
  Register #(.width(32)) R09 (.D(multiplexer_11_out), .en(RegWrite), .Q(O09), .clk(Clk), .clr(Rst));
  Register #(.width(32)) R13 (.D(multiplexer_12_out), .en(RegWrite), .Q(O13), .clk(Clk), .clr(Rst));
  Register #(.width(32)) R17 (.D(multiplexer_13_out), .en(RegWrite), .Q(O17), .clk(Clk), .clr(Rst));
  Register #(.width(32)) R21 (.D(multiplexer_14_out), .en(RegWrite), .Q(O21), .clk(Clk), .clr(Rst));
  Register #(.width(32)) R25 (.D(multiplexer_15_out), .en(RegWrite), .Q(O25), .clk(Clk), .clr(Rst));
  Register #(.width(32)) R29 (.D(multiplexer_16_out), .en(RegWrite), .Q(O29), .clk(Clk), .clr(Rst));
  Register #(.width(32)) R02 (.D(multiplexer_17_out), .en(RegWrite), .Q(O02), .clk(Clk), .clr(Rst));
  Multiplexer #(.width(32), .enable("false")) multiplexer_17 (.in0(O02), .in1(WD), .out(multiplexer_17_out), .sel(I02));
  Register #(.width(32)) R06 (.D(multiplexer_18_out), .en(RegWrite), .Q(O06), .clk(Clk), .clr(Rst));
  Multiplexer #(.width(32), .enable("false")) multiplexer_18 (.in0(O06), .in1(WD), .out(multiplexer_18_out), .sel(I06));
  Register #(.width(32)) R10 (.D(multiplexer_19_out), .en(RegWrite), .Q(O10), .clk(Clk), .clr(Rst));
  Multiplexer #(.width(32), .enable("false")) multiplexer_19 (.in0(O10), .in1(WD), .out(multiplexer_19_out), .sel(I10));
  Register #(.width(32)) R14 (.D(multiplexer_20_out), .en(RegWrite), .Q(O14), .clk(Clk), .clr(Rst));
  Multiplexer #(.width(32), .enable("false")) multiplexer_20 (.in0(O14), .in1(WD), .out(multiplexer_20_out), .sel(I14));
  Multiplexer #(.width(32), .enable("false")) multiplexer_21 (.in0(O18), .in1(WD), .out(multiplexer_21_out), .sel(I18));
  Register #(.width(32)) R18 (.D(multiplexer_21_out), .en(RegWrite), .Q(O18), .clk(Clk), .clr(Rst));
  Register #(.width(32)) R22 (.D(multiplexer_22_out), .en(RegWrite), .Q(O22), .clk(Clk), .clr(Rst));
  Multiplexer #(.width(32), .enable("false")) multiplexer_22 (.in0(O22), .in1(WD), .out(multiplexer_22_out), .sel(I22));
  Register #(.width(32)) R26 (.D(multiplexer_23_out), .en(RegWrite), .Q(O26), .clk(Clk), .clr(Rst));
  Multiplexer #(.width(32), .enable("false")) multiplexer_23 (.in0(O26), .in1(WD), .out(multiplexer_23_out), .sel(I26));
  Multiplexer #(.width(32), .enable("false")) multiplexer_24 (.in0(O30), .in1(WD), .out(multiplexer_24_out), .sel(I30));
  Register #(.width(32)) R30 (.D(multiplexer_24_out), .en(RegWrite), .Q(O30), .clk(Clk), .clr(Rst));
  Multiplexer #(.width(32), .enable("false")) multiplexer_25 (.in0(O03), .in1(WD), .out(multiplexer_25_out), .sel(I03));
  Multiplexer #(.width(32), .enable("false")) multiplexer_26 (.in0(O07), .in1(WD), .out(multiplexer_26_out), .sel(I07));
  Multiplexer #(.width(32), .enable("false")) multiplexer_27 (.in0(O11), .in1(WD), .out(multiplexer_27_out), .sel(I11));
  Multiplexer #(.width(32), .enable("false")) multiplexer_28 (.in0(O15), .in1(WD), .out(multiplexer_28_out), .sel(I15));
  Multiplexer #(.width(32), .enable("false")) multiplexer_29 (.in0(O19), .in1(WD), .out(multiplexer_29_out), .sel(I19));
  Multiplexer #(.width(32), .enable("false")) multiplexer_30 (.in0(O23), .in1(WD), .out(multiplexer_30_out), .sel(I23));
  Multiplexer #(.width(32), .enable("false")) multiplexer_31 (.in0(O27), .in1(WD), .out(multiplexer_31_out), .sel(I27));
  Multiplexer #(.width(32), .enable("false")) multiplexer_32 (.in0(O31), .in1(WD), .out(multiplexer_32_out), .sel(I31));
  Register #(.width(32)) R03 (.D(multiplexer_25_out), .en(RegWrite), .Q(O03), .clk(Clk), .clr(Rst));
  Register #(.width(32)) R07 (.D(multiplexer_26_out), .en(RegWrite), .Q(O07), .clk(Clk), .clr(Rst));
  Register #(.width(32)) R11 (.D(multiplexer_27_out), .en(RegWrite), .Q(O11), .clk(Clk), .clr(Rst));
  Register #(.width(32)) R15 (.D(multiplexer_28_out), .en(RegWrite), .Q(O15), .clk(Clk), .clr(Rst));
  Register #(.width(32)) R19 (.D(multiplexer_29_out), .en(RegWrite), .Q(O19), .clk(Clk), .clr(Rst));
  Register #(.width(32)) R23 (.D(multiplexer_30_out), .en(RegWrite), .Q(O23), .clk(Clk), .clr(Rst));
  Register #(.width(32)) R27 (.D(multiplexer_31_out), .en(RegWrite), .Q(O27), .clk(Clk), .clr(Rst));
  Register #(.width(32)) R31 (.D(multiplexer_32_out), .en(RegWrite), .Q(O31), .clk(Clk), .clr(Rst));
  Decoder #(.select(5), .enable("false")) decoder_1 (
    .out0(I00), .out1(I01), .out2(I02), .out3(I03), .out4(I04), .out5(I05), .out6(I06), .out7(I07),
    .out8(I08), .out9(I09), .out10(I10), .out11(I11), .out12(I12), .out13(I13), .out14(I14), .out15(I15),
    .out16(I16), .out17(I17), .out18(I18), .out19(I19), .out20(I20), .out21(I21), .out22(I22), .out23(I23),
    .out24(I24), .out25(I25), .out26(I26), .out27(I27), .out28(I28), .out29(I29), .out30(I30), .out31(I31),
    .sel(A3));
  Multiplexer #(.select(5), .width(32), .enable("false")) multiplexer_33 (
    .in0(O00), .in1(O01), .in2(O02), .in3(O03), .in4(O04), .in5(O05), .in6(O06), .in7(O07), .in8(O08),
    .in9(O09), .in10(O10), .in11(O11), .in12(O12), .in13(O13), .in14(O14), .in15(O15), .in16(O16),
    .in17(O17), .in18(O18), .in19(O19), .in20(O20), .in21(O21), .in22(O22), .in23(O23), .in24(O24),
    .in25(O25), .in26(O26), .in27(O27), .in28(O28), .in29(O29), .in30(O30), .in31(O31), .out(RD2), .sel(A2));
  Multiplexer #(.select(5), .width(32), .enable("false")) multiplexer_34 (
    .in0(O00), .in1(O01), .in2(O02), .in3(O03), .in4(O04), .in5(O05), .in6(O06), .in7(O07), .in8(O08),
    .in9(O09), .in10(O10), .in11(O11), .in12(O12), .in13(O13), .in14(O14), .in15(O15), .in16(O16),
    .in17(O17), .in18(O18), .in19(O19), .in20(O20), .in21(O21), .in22(O22), .in23(O23), .in24(O24),
    .in25(O25), .in26(O26), .in27(O27), .in28(O28), .in29(O29), .in30(O30), .in31(O31), .out(RD1), .sel(A1));
endmodule

module IFU (
  input  Clk,
  input  PCSrc,
  input  Jump,
  input  Rst,
  input  [31:0] SignImm,
  input  [25:0] JumpAddr,
  output [31:0] pc,
  output [31:0] Instr
);

  wire [3:0] adder_1_out;
  wire [27:0] adder_1_out_2, bit_extender_1_out, shifter_2_out;
  wire [31:0] adder_2_out, multiplexer_1_out, multiplexer_2_out, shifter_1_out;

  Multiplexer #(.width(32), .enable("false")) multiplexer_1 (
    .in0({adder_1_out, adder_1_out_2}), .in1(adder_2_out), .out(multiplexer_1_out), .sel(PCSrc));
  Multiplexer #(.width(32), .enable("false")) multiplexer_2 (
    .in0(multiplexer_1_out), .in1({adder_1_out, shifter_2_out}), .out(multiplexer_2_out), .sel(Jump));
  PC pc_1 (.Addr_prime(multiplexer_2_out), .Clk(Clk), .Rst(Rst), .Addr(pc));
  assign bit_extender_1_out = {{2{1'b0}}, JumpAddr};  // Bit_Extender bit_extender_1
  Adder #(.width(32)) adder_1 (.a(pc), .b(32'h4), .out({adder_1_out, adder_1_out_2}));  // open: cin, cout
  Shifter #(.width(32)) shifter_1 (.in(SignImm), .\dist (5'b00010), .out(shifter_1_out));
  Shifter #(.width(28)) shifter_2 (.in(bit_extender_1_out), .\dist (5'b00010), .out(shifter_2_out));
  IM im_1 (.Addr(pc), .Instr(Instr));
  Adder #(.width(32)) adder_2 (
    .a({adder_1_out, adder_1_out_2}), .b(shifter_1_out), .out(adder_2_out));  // open: cin, cout
endmodule

module PC (
  input  [31:0] Addr_prime,
  input  Clk,
  input  Rst,
  output [31:0] Addr
);

  wire [31:0] multiplexer_1_out, register_1_q;

  Multiplexer #(.width(32), .enable("false")) multiplexer_1 (
    .in0(Addr_prime), .in1(32'h3000), .out(multiplexer_1_out), .sel(Rst));
  Register #(.width(32)) register_1 (.D(multiplexer_1_out), .Q(register_1_q), .clk(Clk));  // open: en, clr
  Multiplexer #(.width(32), .enable("false")) multiplexer_2 (.in0(register_1_q), .in1(32'h3000), .out(Addr), .sel(Rst));
endmodule

module IM (
  input  [31:0] Addr,
  output [31:0] Instr
);

  wire [31:0] subtractor_1_out;

  Subtractor #(.width(32)) subtractor_1 (.a(Addr), .b(32'h3000), .out(subtractor_1_out));  // open: bin, bout
  ROM #(.addrWidth(12), .dataWidth(32)) rom_1 (.addr(subtractor_1_out[13:2]), .data(Instr));  // open: sel

  // Notes on the sheet:
  //   contents of rom_1 (hex, n*v repeats v):
  //   34000001 34010001 34020001 34030001 34040001 34050001 34060001 34070001 34080001 34090001 340a0001
  //   340b0001 340c0001 340d0001 340e0001 340f0001 34100001 34110001 34120001 34130001 34140001 34150001
  //   34160001 34170001 34180001 34190001 341a0001 341b0001 341c0001 341d0001 341e0001 341f0001 3404007b
  //   348501c8 3c06007b 3c07ffff 34e7ffff 868020 878820 e79020 34080000 ad040000 ad050004 ad060008
  //   ad07000c ad100010 ad110014 ad120018 8d040000 8d05000c ad04001c ad050020 34040001 34050002 34060001
  //   10850001 10860001 ad040024 ad050028
endmodule

module ALU (
  input  [31:0] SrcA,
  input  [31:0] SrcB,
  input  [2:0] ALUCtrl,
  input  [4:0] Shamt,
  output [31:0] ALURes,
  output Zero
);

  wire [31:0] Add, Or, sll, Sub, Xor;

  assign Or = SrcA | SrcB;  // OR_Gate or_1, 32 bits wide
  Adder #(.width(32)) adder_1 (.a(SrcA), .b(SrcB), .out(Add));  // open: cin, cout
  Subtractor #(.width(32)) subtractor_1 (.a(SrcA), .b(SrcB), .out(Sub));  // open: bin, bout
  Shifter #(.width(32)) shifter_1 (.in(SrcA), .\dist (Shamt), .out(sll));
  assign Xor = SrcA ^ SrcB;  // XOR_Gate xor_1, 32 bits wide
  Multiplexer #(.select(3), .width(32), .enable("false")) multiplexer_1 (
    .in0(sll), .in1(Or), .in2(Add), .in4(Sub), .in6(Xor), .out(ALURes), .sel(ALUCtrl));  // open: in3, in5, in7
  Comparator #(.width(32), .mode("unsigned")) comparator_1 (.a(ALURes), .b({32{1'b0}}), .eq(Zero));  // open: gt, lt

  // Other names for the same wires on the sheet: A[31:0] = SrcA; B[31:0] = SrcB
endmodule

module ALUC (
  input  [2:0] ALUCtrl,
  input  [31:0] SrcA,
  input  [31:0] Dat,
  input  [31:0] SignImm,
  input  ALUSrc,
  input  [4:0] Shamt,
  output Zero,
  output [31:0] ALURes
);

  wire [31:0] multiplexer_1_out;

  ALU alu_1 (.SrcA(SrcA), .SrcB(multiplexer_1_out), .Shamt(Shamt), .ALURes(ALURes), .Zero(Zero), .ALUCtrl(ALUCtrl));
  Multiplexer #(.width(32), .enable("false")) multiplexer_1 (
    .in0(Dat), .in1(SignImm), .out(multiplexer_1_out), .sel(ALUSrc));
endmodule

module DM (
  input  [11:0] Addr,
  input  [31:0] WriteData,
  input  Clk,
  input  WE,
  input  Rst,
  input  isByte,
  input  [1:0] \byte ,
  output [31:0] ReadData
);

  wire [31:0] multiplexer_1_out, multiplexer_2_out;

  Multiplexer #(.select(2), .width(32), .enable("false")) multiplexer_1 (
    .in0({ReadData[31:8], WriteData[7:0]}), .in1({ReadData[31:16], WriteData[7:0], ReadData[7:0]}),
    .in2({ReadData[31:24], WriteData[7:0], ReadData[15:0]}), .in3({WriteData[7:0], ReadData[23:0]}),
    .out(multiplexer_1_out), .sel(\byte ));
  Multiplexer #(.width(32), .enable("false")) multiplexer_2 (
    .in0(WriteData), .in1(multiplexer_1_out), .out(multiplexer_2_out), .sel(isByte));
  RAM #(.addrWidth(12), .dataWidth(32), .bus("separate")) ram_1 (
    .addr(Addr), .din(multiplexer_2_out), .data(ReadData), .str(WE), .clk(Clk), .ld(1'b1), .clr(Rst));  // open: sel
endmodule

module DMC (
  input  isByte,
  input  jal,
  input  MemtoReg,
  input  Clk,
  input  MemWrite,
  input  [31:0] ALURes,
  input  [31:0] WriteData,
  input  Rst,
  input  [31:0] PC,
  output [31:0] Addr,
  output [31:0] Result
);

  wire and_1_out;
  wire [7:0] multiplexer_1_out;
  wire [31:0] adder_1_out, bit_extender_1_out, dm_1_readdata, multiplexer_2_out, multiplexer_4_out;

  DM dm_1 (
    .WriteData(WriteData), .Clk(Clk), .WE(MemWrite), .Rst(Rst), .ReadData(dm_1_readdata), .isByte(isByte),
    .Addr(ALURes[13:2]), .\byte (ALURes[1:0]));
  and and_1 (and_1_out, isByte, MemtoReg);
  Multiplexer #(.select(2), .width(8), .enable("false")) multiplexer_1 (
    .in0(dm_1_readdata[7:0]), .in1(dm_1_readdata[15:8]), .in2(dm_1_readdata[23:16]),
    .in3(dm_1_readdata[31:24]), .out(multiplexer_1_out), .sel(ALURes[1:0]));
  Adder #(.width(32)) adder_1 (.a(PC), .b(32'h4), .out(adder_1_out));  // open: cin, cout
  Multiplexer #(.width(32), .enable("false")) multiplexer_2 (
    .in0(ALURes), .in1(multiplexer_4_out), .out(multiplexer_2_out), .sel(MemtoReg));
  Multiplexer #(.width(32), .enable("false")) multiplexer_3 (
    .in0(multiplexer_2_out), .in1(adder_1_out), .out(Result), .sel(jal));
  Multiplexer #(.width(32), .enable("false")) multiplexer_4 (
    .in0(dm_1_readdata), .in1(bit_extender_1_out), .out(multiplexer_4_out), .sel(and_1_out));
  assign bit_extender_1_out = {{24{multiplexer_1_out[7]}}, multiplexer_1_out};  // Bit_Extender bit_extender_1

  assign Addr = ALURes;
endmodule

module EXT (
  input  [15:0] Imm,
  input  [1:0] ExtOp,
  output [31:0] ExtImm
);

  wire [31:0] bit_extender_1_out, bit_extender_2_out, shifter_1_out;

  assign bit_extender_1_out = {{16{1'b0}}, Imm};  // Bit_Extender bit_extender_1
  assign bit_extender_2_out = {{16{Imm[15]}}, Imm};  // Bit_Extender bit_extender_2
  Shifter #(.width(32)) shifter_1 (.in(bit_extender_1_out), .\dist (5'b10000), .out(shifter_1_out));
  Multiplexer #(.select(2), .width(32), .enable("false")) multiplexer_1 (
    .in0(bit_extender_1_out), .in1(bit_extender_2_out), .in2(shifter_1_out), .out(ExtImm), .sel(ExtOp));  // open: in3
endmodule

// Ctrler
module CU (
  input  [5:0] funct,
  input  [5:0] Opcode,
  input  Zero,
  output isByte,
  output PCSrc,
  output [2:0] ALUCtrl,
  output jal,
  output [1:0] EXTOp,
  output RegWrite,
  output RegDst,
  output ALUSrc,
  output MemWrite,
  output MemtoReg,
  output Jump
);

  wire add_out, beq_out, lb_out, lui_out, lw_out, not_1_out, not_2_out, not_3_out, not_4_out, not_5_out,
       not_6_out, not_7_out, not_8_out, not_9_out, not_10_out, not_11_out, not_12_out, or_3_out, ori_out, R,
       sb_out, sub_out, sw_out, xor_out;

  not not_1 (not_1_out, Opcode[5]);
  not not_2 (not_2_out, Opcode[2]);
  not not_3 (not_3_out, Opcode[4]);
  not not_4 (not_4_out, Opcode[3]);
  not not_5 (not_5_out, Opcode[1]);
  not not_6 (not_6_out, Opcode[0]);
  and u_R (R, not_1_out, not_3_out, not_4_out, not_2_out, not_5_out, not_6_out);
  and lw (lw_out, Opcode[5], not_3_out, not_4_out, not_2_out, Opcode[1], Opcode[0]);
  and sw (sw_out, Opcode[5], not_3_out, Opcode[3], not_2_out, Opcode[1], Opcode[0]);
  and beq (beq_out, not_1_out, not_3_out, not_4_out, Opcode[2], not_5_out, not_6_out);
  and ori (ori_out, not_1_out, not_3_out, Opcode[3], Opcode[2], not_5_out, Opcode[0]);
  and lui (lui_out, not_1_out, not_3_out, Opcode[3], Opcode[2], Opcode[1], Opcode[0]);
  and j (jal, not_1_out, not_3_out, not_4_out, not_2_out, Opcode[1], not_6_out);
  and u_jal (jal, not_1_out, not_3_out, not_4_out, not_2_out, Opcode[1], Opcode[0]);
  and lb (lb_out, Opcode[5], not_3_out, not_4_out, not_2_out, not_5_out, not_6_out);
  and sb (sb_out, Opcode[5], not_3_out, Opcode[3], not_2_out, not_5_out, not_6_out);
  or or_1 (RegWrite, R, lw_out, ori_out, lui_out, jal, lb_out);
  buf or_2 (RegDst, R);  // OR_Gate
  and and_1 (PCSrc, Zero, or_3_out);
  buf or_3 (or_3_out, beq_out);  // OR_Gate
  or or_4 (ALUSrc, lw_out, sw_out, ori_out, lui_out, lb_out, sb_out);
  or or_5 (MemWrite, sw_out, sb_out);
  or or_6 (MemtoReg, lw_out, lb_out);
  buf or_7 (EXTOp[1], lui_out);  // OR_Gate
  or or_8 (isByte, lb_out, sb_out);
  or or_9 (EXTOp[0], lw_out, sw_out, beq_out, lb_out, sb_out);
  buf or_10 (Jump, jal);  // OR_Gate
  or or_11 (ALUCtrl[2], sub_out, beq_out, xor_out);
  or or_12 (ALUCtrl[1], add_out, lw_out, sw_out, xor_out, lb_out);
  or or_13 (ALUCtrl[0], ori_out, lui_out, jal);
  and add (add_out, funct[5], not_8_out, not_10_out, R, not_9_out, not_11_out, not_12_out);
  and sub (sub_out, funct[5], not_8_out, not_10_out, R, not_9_out, funct[1], not_12_out);
  and \xor  (xor_out, funct[5], not_8_out, not_10_out, R, funct[2], funct[1], not_12_out);
  not not_7 (not_7_out, funct[5]);
  not not_8 (not_8_out, funct[4]);
  not not_9 (not_9_out, funct[2]);
  not not_10 (not_10_out, funct[3]);
  not not_11 (not_11_out, funct[1]);
  not not_12 (not_12_out, funct[0]);
endmodule

module Splitter (
  input  [31:0] Instr,
  output [15:0] imm,
  output [25:0] addr,
  output [5:0] funct,
  output [4:0] shamt,
  output [4:0] rd,
  output [4:0] rt,
  output [4:0] rs,
  output [5:0] Opcode
);


  assign addr = Instr[25:0];
  assign funct = Instr[5:0];
  assign imm = Instr[15:0];
  assign Opcode = Instr[31:26];
  assign rd = Instr[15:11];
  assign rs = Instr[25:21];
  assign rt = Instr[20:16];
  assign shamt = Instr[10:6];
endmodule
