// Logisim project _fibonacci_1.circ as structural Verilog: 1 circuit, main circuit main
module main (
  input  [2:0] N,
  output [3:0] Nth
);

  wire clock_1_out, comparator_1_eq, comparator_1_gt, comparator_2_eq;
  wire [2:0] C1_q;
  wire [3:0] adder_1_out, bit_extender_1_out, multiplexer_2_out, multiplexer_3_out, R0_q, R1_q;

  Comparator #(.width(3), .mode("unsigned")) comparator_1 (
    .a(N), .b(C1_q), .gt(comparator_1_gt), .eq(comparator_1_eq));  // open: lt
  Comparator #(.width(3), .mode("unsigned")) comparator_2 (.a(C1_q), .b(3'b000), .eq(comparator_2_eq));  // open: gt, lt
  Multiplexer #(.width(4), .enable("false")) multiplexer_1 (
    .in0(4'b0000), .in1(R1_q), .out(Nth), .sel(comparator_1_eq));
  Adder #(.width(4)) adder_1 (.a(R0_q), .b(R1_q), .out(adder_1_out));  // open: cin, cout
  assign bit_extender_1_out = {{3{1'b0}}, comparator_2_eq};  // Bit_Extender bit_extender_1
  Multiplexer #(.width(4), .enable("false")) multiplexer_2 (
    .in0(R1_q), .in1(4'b0000), .out(multiplexer_2_out), .sel(comparator_2_eq));
  Multiplexer #(.width(4), .enable("false")) multiplexer_3 (
    .in0(adder_1_out), .in1(bit_extender_1_out), .out(multiplexer_3_out), .sel(comparator_2_eq));
  Counter #(.width(3), .max('h7)) C1 (
    .D(3'b000), .count(comparator_1_gt), .Q(C1_q), .clk(clock_1_out));  // open: load, carry, clr
  Register #(.width(4)) R0 (.D(multiplexer_2_out), .en(comparator_1_gt), .Q(R0_q), .clk(clock_1_out));  // open: clr
  Register #(.width(4)) R1 (.D(multiplexer_3_out), .en(comparator_1_gt), .Q(R1_q), .clk(clock_1_out));  // open: clr
  Clock clock_1 (.out(clock_1_out));
endmodule
