// Logisim project _fibonacci_2.circ as structural Verilog: 3 circuits, main circuit main
module main (
  input  [31:0] in_1,
  output [31:0] out_2
);

  wire and_1_out, and_2_out, bitselector_1_out, clock_1_out, comparator_1_eq, comparator_1_gt,
       comparator_2_eq, counter_1_q, or_1_out, or_2_out;
  wire [31:0] ans_1_1_q, ans_1_2_q, b_q, base_1_1_q, base_1_2_q, base_2_1_q, base_2_2_q, multiplexer_1_out,
       multiplexer_2_out, multiplexer_3_out, multiplexer_4_out, multiplexer_5_out, multiplexer_6_out,
       multiplexer_7_out, multiplexer_8_out, multiplexer_9_out, multiplexer_10_out, multiplexer_11_out,
       n1x2x2x2_matrix_1_c_1_1, n1x2x2x2_matrix_1_c_1_2, n2x2x2x2_matrix_1_c_1_1, n2x2x2x2_matrix_1_c_1_2,
       n2x2x2x2_matrix_1_c_2_1, n2x2x2x2_matrix_1_c_2_2, shifter_1_out, subtractor_1_out;

  BitSelector #(.width(32)) bitselector_1 (.in(b_q), .out(bitselector_1_out), .sel({5{1'b0}}));
  Subtractor #(.width(32)) subtractor_1 (.a(in_1), .b(32'h2), .out(subtractor_1_out));  // open: bin, bout
  Comparator #(.width(32), .mode("unsigned")) comparator_1 (
    .a(in_1), .b(32'h2), .gt(comparator_1_gt), .eq(comparator_1_eq));  // open: lt
  _2x2x2x2_matrix u_2x2x2x2_matrix_1 (
    .a_1_1(base_1_1_q), .a_1_2(base_1_2_q), .a_2_1(base_2_1_q), .a_2_2(base_2_2_q), .b_1_1(base_1_1_q),
    .b_1_2(base_1_2_q), .b_2_1(base_2_1_q), .b_2_2(base_2_2_q), .c_1_1(n2x2x2x2_matrix_1_c_1_1),
    .c_1_2(n2x2x2x2_matrix_1_c_1_2), .c_2_1(n2x2x2x2_matrix_1_c_2_1), .c_2_2(n2x2x2x2_matrix_1_c_2_2));
  Multiplexer #(.width(32), .enable("false")) multiplexer_1 (
    .in0(32'h1), .in1(base_1_1_q), .out(multiplexer_1_out), .sel(bitselector_1_out));
  Multiplexer #(.width(32), .enable("false")) multiplexer_2 (
    .in0({32{1'b0}}), .in1(base_1_2_q), .out(multiplexer_2_out), .sel(bitselector_1_out));
  Multiplexer #(.width(32), .enable("false")) multiplexer_3 (
    .in0({32{1'b0}}), .in1(base_2_1_q), .out(multiplexer_3_out), .sel(bitselector_1_out));
  Multiplexer #(.width(32), .enable("false")) multiplexer_4 (
    .in0(32'h1), .in1(base_2_2_q), .out(multiplexer_4_out), .sel(bitselector_1_out));
  Comparator #(.width(32), .mode("unsigned")) comparator_2 (
    .a(b_q), .b({32{1'b0}}), .eq(comparator_2_eq));  // open: gt, lt
  or or_1 (or_1_out, comparator_1_gt, comparator_1_eq);
  _1x2x2x2_matrix u_1x2x2x2_matrix_1 (
    .a_1_1(ans_1_1_q), .a_1_2(ans_1_2_q), .b_1_1(multiplexer_1_out), .b_1_2(multiplexer_2_out),
    .b_2_1(multiplexer_3_out), .b_2_2(multiplexer_4_out), .c_1_1(n1x2x2x2_matrix_1_c_1_1),
    .c_1_2(n1x2x2x2_matrix_1_c_1_2));
  Shifter #(.width(32), .shift("lr")) shifter_1 (.in(b_q), .\dist (5'b00001), .out(shifter_1_out));
  Multiplexer #(.width(32), .enable("false")) multiplexer_5 (
    .in0(32'h1), .in1(n2x2x2x2_matrix_1_c_1_1), .out(multiplexer_5_out), .sel(counter_1_q));
  Multiplexer #(.width(32), .enable("false")) multiplexer_6 (
    .in0(32'h1), .in1(n2x2x2x2_matrix_1_c_1_2), .out(multiplexer_6_out), .sel(counter_1_q));
  Multiplexer #(.width(32), .enable("false")) multiplexer_7 (
    .in0(32'h1), .in1(n2x2x2x2_matrix_1_c_2_1), .out(multiplexer_7_out), .sel(counter_1_q));
  Multiplexer #(.width(32), .enable("false")) multiplexer_8 (
    .in0({32{1'b0}}), .in1(n2x2x2x2_matrix_1_c_2_2), .out(multiplexer_8_out), .sel(counter_1_q));
  Multiplexer #(.width(32), .enable("false")) multiplexer_9 (
    .in0(32'h1), .in1(n1x2x2x2_matrix_1_c_1_1), .out(multiplexer_9_out), .sel(counter_1_q));
  Multiplexer #(.width(32), .enable("false")) multiplexer_10 (
    .in0(32'h1), .in1(n1x2x2x2_matrix_1_c_1_2), .out(multiplexer_10_out), .sel(counter_1_q));
  Multiplexer #(.width(32), .enable("false")) multiplexer_11 (
    .in0(subtractor_1_out), .in1(shifter_1_out), .out(multiplexer_11_out), .sel(counter_1_q));
  or or_2 (or_2_out, ~counter_1_q, and_1_out);  // OR_Gate
  Clock clock_1 (.out(clock_1_out));
  and and_1 (and_1_out, or_1_out, ~comparator_2_eq);  // AND_Gate
  Counter #(.width(1), .max('h1), .ongoal("stay")) counter_1 (
    .count(or_2_out), .Q(counter_1_q), .clk(clock_1_out));  // open: load, D, carry, clr
  Register #(.width(32)) base_1_1 (
    .D(multiplexer_5_out), .en(or_2_out), .Q(base_1_1_q), .clk(clock_1_out));  // open: clr
  Register #(.width(32)) base_1_2 (
    .D(multiplexer_6_out), .en(or_2_out), .Q(base_1_2_q), .clk(clock_1_out));  // open: clr
  Register #(.width(32)) base_2_1 (
    .D(multiplexer_7_out), .en(or_2_out), .Q(base_2_1_q), .clk(clock_1_out));  // open: clr
  Register #(.width(32)) base_2_2 (
    .D(multiplexer_8_out), .en(or_2_out), .Q(base_2_2_q), .clk(clock_1_out));  // open: clr
  Register #(.width(32)) ans_1_1 (.D(multiplexer_9_out), .en(or_2_out), .Q(ans_1_1_q), .clk(clock_1_out));  // open: clr
  Register #(.width(32)) ans_1_2 (
    .D(multiplexer_10_out), .en(or_2_out), .Q(ans_1_2_q), .clk(clock_1_out));  // open: clr
  Register #(.width(32)) b (.D(multiplexer_11_out), .en(or_1_out), .Q(b_q), .clk(clock_1_out));  // open: clr
  and and_2 (and_2_out, comparator_2_eq, or_1_out);
  Multiplexer #(.width(32), .enable("false")) multiplexer_12 (
    .in0({32{1'b0}}), .in1(ans_1_1_q), .out(out_2), .sel(and_2_out));
endmodule

module _1x2x2x2_matrix (
  input  [31:0] a_1_1,
  input  [31:0] a_1_2,
  input  [31:0] b_1_1,
  input  [31:0] b_1_2,
  input  [31:0] b_2_1,
  input  [31:0] b_2_2,
  output [31:0] c_1_1,
  output [31:0] c_1_2
);

  wire [31:0] multiplier_1_out, multiplier_2_out, multiplier_3_out, multiplier_4_out;

  Multiplier #(.width(32)) multiplier_1 (.a(a_1_1), .b(b_1_1), .out(multiplier_1_out));  // open: cin, cout
  Multiplier #(.width(32)) multiplier_2 (.a(a_1_2), .b(b_2_1), .out(multiplier_2_out));  // open: cin, cout
  Multiplier #(.width(32)) multiplier_3 (.a(a_1_1), .b(b_1_2), .out(multiplier_3_out));  // open: cin, cout
  Multiplier #(.width(32)) multiplier_4 (.a(a_1_2), .b(b_2_2), .out(multiplier_4_out));  // open: cin, cout
  Adder #(.width(32)) adder_1 (.a(multiplier_1_out), .b(multiplier_2_out), .out(c_1_1));  // open: cin, cout
  Adder #(.width(32)) adder_2 (.a(multiplier_3_out), .b(multiplier_4_out), .out(c_1_2));  // open: cin, cout
endmodule

module _2x2x2x2_matrix (
  input  [31:0] a_1_1,
  input  [31:0] a_1_2,
  input  [31:0] a_2_1,
  input  [31:0] a_2_2,
  input  [31:0] b_1_1,
  input  [31:0] b_1_2,
  input  [31:0] b_2_1,
  input  [31:0] b_2_2,
  output [31:0] c_1_1,
  output [31:0] c_1_2,
  output [31:0] c_2_1,
  output [31:0] c_2_2
);

  wire [31:0] multiplier_1_out, multiplier_2_out, multiplier_3_out, multiplier_4_out, multiplier_5_out,
       multiplier_6_out, multiplier_7_out, multiplier_8_out;

  Multiplier #(.width(32)) multiplier_1 (.a(a_1_1), .b(b_1_1), .out(multiplier_1_out));  // open: cin, cout
  Multiplier #(.width(32)) multiplier_2 (.a(a_1_2), .b(b_2_1), .out(multiplier_2_out));  // open: cin, cout
  Multiplier #(.width(32)) multiplier_3 (.a(a_1_1), .b(b_1_2), .out(multiplier_3_out));  // open: cin, cout
  Multiplier #(.width(32)) multiplier_4 (.a(a_1_2), .b(b_2_2), .out(multiplier_4_out));  // open: cin, cout
  Multiplier #(.width(32)) multiplier_5 (.a(a_2_1), .b(b_1_1), .out(multiplier_5_out));  // open: cin, cout
  Multiplier #(.width(32)) multiplier_6 (.a(a_2_2), .b(b_2_1), .out(multiplier_6_out));  // open: cin, cout
  Multiplier #(.width(32)) multiplier_7 (.a(a_2_1), .b(b_1_2), .out(multiplier_7_out));  // open: cin, cout
  Multiplier #(.width(32)) multiplier_8 (.a(a_2_2), .b(b_2_2), .out(multiplier_8_out));  // open: cin, cout
  Adder #(.width(32)) adder_1 (.a(multiplier_1_out), .b(multiplier_2_out), .out(c_1_1));  // open: cin, cout
  Adder #(.width(32)) adder_2 (.a(multiplier_3_out), .b(multiplier_4_out), .out(c_1_2));  // open: cin, cout
  Adder #(.width(32)) adder_3 (.a(multiplier_5_out), .b(multiplier_6_out), .out(c_2_1));  // open: cin, cout
  Adder #(.width(32)) adder_4 (.a(multiplier_7_out), .b(multiplier_8_out), .out(c_2_2));  // open: cin, cout
endmodule
