// Logisim project _mod5.circ as structural Verilog: 1 circuit, main circuit mod5
module mod5 (
  input  In,
  output S0,
  output S1,
  output S2,
  output S3,
  output S4
);

  wire and_1_out, and_2_out, and_3_out, and_4_out, and_5_out, and_6_out, clock_1_out;
  wire [1:0] or_2_out, register_1_q;
  wire [2:0] bit_extender_1_out;

  and and_1 (and_1_out, ~register_1_q[0], register_1_q[1]);  // AND_Gate
  and and_2 (and_2_out, register_1_q[0], ~register_1_q[1]);  // AND_Gate
  and and_3 (and_3_out, ~register_1_q[0], ~register_1_q[1], In);  // AND_Gate
  and and_4 (and_4_out, ~register_1_q[0], register_1_q[1], ~In);  // AND_Gate
  and and_5 (and_5_out, register_1_q[0], ~register_1_q[1], ~In);  // AND_Gate
  and and_6 (and_6_out, register_1_q[0], register_1_q[1], In);
  or or_1 (or_2_out[0], and_1_out, and_2_out);
  or or_2 (or_2_out[1], and_3_out, and_4_out, and_5_out, and_6_out);
  Register #(.width(2)) register_1 (.D(or_2_out), .en(1'b1), .Q(register_1_q), .clk(clock_1_out));  // open: clr
  Clock clock_1 (.out(clock_1_out));
  Demultiplexer #(.select(3), .enable("false")) demultiplexer_1 (
    .out3(S0), .out4(S1), .out5(S2), .out6(S3), .out7(S4), .in(1'b1), .sel(bit_extender_1_out));  // open: out0, out1, out2
  // Probe on bit_extender_1_out
  assign bit_extender_1_out = {{1{1'b1}}, {or_2_out[0], or_2_out[1]}};  // Bit_Extender bit_extender_1

  // Notes on the sheet:
  //   x0
  //   x1
  //   x0'
  //   x1'
  //   x1
  //   x0
endmodule
